// Logisim project Simple CPU.circ as structural Verilog: 3 circuits, main circuit main
module main (
  input  [7:0] in_1,
  input  [1:0] in_2,
  input  F2,
  input  F1,
  input  F0
);

  wire clock_1_out;
  wire [7:0] alu_1_c, MBR, multiplexer_1_out, register_1_q, register_2_q, register_3_q, register_4_q;

  Counter counter_1 (.D(alu_1_c), .Q(MBR), .clk(clock_1_out));  // open: load, count, carry, clr
  Register register_1 (.D(alu_1_c), .Q(register_1_q), .clk(clock_1_out));  // open: en, clr
  Register register_2 (.D(alu_1_c), .Q(register_2_q), .clk(clock_1_out));  // open: en, clr
  Register register_3 (.D(alu_1_c), .Q(register_3_q), .clk(clock_1_out));  // open: en, clr
  Clock clock_1 (.out(clock_1_out));
  Register register_4 (.D(MBR), .Q(register_4_q), .clk(clock_1_out));  // open: en, clr
  Hex_Digit_Display hex_digit_display_1 (.value(register_1_q[3:0]));  // open: dp
  Hex_Digit_Display hex_digit_display_2 (.value(register_1_q[7:4]));  // open: dp
  Multiplexer #(.select(2), .width(8), .enable("false")) multiplexer_1 (
    .in0(register_2_q), .in1(register_4_q), .in2(MBR), .in3(in_1), .out(multiplexer_1_out), .sel(in_2));
  ALU alu_1 (.A(register_3_q), .B(multiplexer_1_out), .C(alu_1_c), .F2(F2), .F1(F1), .F0(F0));
endmodule

module ALU (
  input  [7:0] A,
  input  [7:0] B,
  input  F2,
  input  F1,
  input  F0,
  output [7:0] C
);

  wire [7:0] adder_1_out, adder_2_out, adder_3_out, and_1_out, or_1_out, subtractor_1_out;

  Adder adder_1 (.a(A), .b(8'h1), .out(adder_1_out));  // open: cin, cout
  Adder adder_2 (.a(B), .b(8'h1), .out(adder_2_out));  // open: cin, cout
  Adder adder_3 (.a(A), .b(B), .out(adder_3_out));  // open: cin, cout
  Subtractor subtractor_1 (.a(A), .b(B), .out(subtractor_1_out));  // open: bin, bout
  assign and_1_out = A & B;  // AND_Gate and_1, 8 bits wide
  assign or_1_out = A | B;  // OR_Gate or_1, 8 bits wide
  Multiplexer #(.select(3), .width(8), .enable("false")) multiplexer_1 (
    .in0(A), .in1(B), .in2(adder_1_out), .in3(adder_2_out), .in4(adder_3_out), .in5(subtractor_1_out),
    .in6(and_1_out), .in7(or_1_out), .out(C), .sel({F2, F1, F0}));

  // Notes on the sheet:
  //   B
  //   A
  //   1
endmodule

module Control_Unit (
  input  [4:0] From_MBR,
  output [2:0] ALU_control,
  output [4:0] Register_write_control,
  output [1:0] ALU_B_Bus_Select
);

  wire clock_1_out, JMPC;
  wire [4:0] MIR_q, MPC_q, multiplexer_1_out;
  wire [15:0] rom_1_data;

  Multiplexer #(.width(5), .enable("false")) multiplexer_1 (
    .in0(MIR_q), .in1(From_MBR), .out(multiplexer_1_out), .sel(JMPC));
  Register #(.width(5)) MPC (.D(multiplexer_1_out), .Q(MPC_q), .clk(clock_1_out));  // open: en, clr
  ROM #(.addrWidth(5), .dataWidth(16)) rom_1 (.addr(MPC_q), .data(rom_1_data));  // open: sel
  Register #(.width(16)) MIR (
    .D(rom_1_data), .Q({ALU_B_Bus_Select, Register_write_control, ALU_control, JMPC, MIR_q}),
    .clk(clock_1_out));  // open: en, clr
  Clock clock_1 (.out(clock_1_out));

  // Notes on the sheet:
  //   Microprogram Control Store
endmodule
